# Fritzing sketch simple-traffic-light (saved by Fritzing 0.9.3b)
breadboards: 1

parts:
  Componente1 = Arduino Uno (Rev3)
  R1 = Resistor [tolerance=±5% resistance=220 package=THT]
  R2 = Resistor [tolerance=±5% resistance=220 package=THT]
  R3 = Resistor [tolerance=±5% resistance=220 package=THT]
  LED1 = LED - 5mm [color="Red (633nm)" package="5 mm [THT]"]
  LED2 = LED - 5mm [color="Red (633nm)" package="5 mm [THT]"]
  LED3 = LED - 5mm [color="Red (633nm)" package="5 mm [THT]"]

nets:
  N1: Componente1.D9_PWM, R1.Pin_0
  N2: Componente1.GND, LED1.anode, LED2.anode, LED3.anode
  N3: Componente1.D0/RX, R3.Pin_0
  N4: Componente1.D5_PWM, R2.Pin_0
  N5: R1.Pin_1, LED1.cathode
  N6: R2.Pin_1, LED2.cathode
  N7: R3.Pin_1, LED3.cathode

// code stored in the sketch: semaforo.ino
void setup () {
pinMode(9,OUTPUT);// LED Rojo
pinMode(5,OUTPUT);// LED Amarillo
pinMode(0,OUTPUT);// LED Verde
}

void loop () {
  digitalWrite(9,HIGH);//Enciendo Rojo
  delay(5000);//Queda encendido 2 segundos
  digitalWrite(9,LOW);//Apago Rojo
  
  digitalWrite(0,HIGH);//Enciendo Verde
  delay(5000);//Queda encendido 2 segundos
  digitalWrite(0,LOW);//Apago Verde
  
  digitalWrite(5,HIGH);//Enciendo Ámbar
  delay(1000);//Queda encendido 1 segundo
  digitalWrite(5,LOW);//Apago Rojo
}
