# Fritzing sketch contador-display-7segmentos (saved by Fritzing 0.9.3b)
breadboards: 1

parts:
  Componente1 = Arduino Uno (Rev3)
  U1 = 7-SEGMENT-DISPLAY [package=7-segment-display]
  R1 = Resistor [tolerance=±5% resistance=220 package=THT]

nets:
  N1: Componente1.D8, U1.G1
  N2: Componente1.D9_PWM, U1.D
  N3: Componente1.D10_PWM/SS, U1.A
  N4: Componente1.D11_PWM/MOSI, U1.G2
  N5: Componente1.D12/MISO, U1.G
  N6: Componente1.D13/SCK, U1.E
  N7: Componente1.GND, R1.Pin_1
  N8: Componente1.D7, U1.DP
  N9: U1.C, R1.Pin_0
