# Fritzing sketch dual_display7segment_v2 (saved by Fritzing 0.9.3b)
circuit board: 8.46667cm x 5.64444cm
breadboards: 2

parts:
  U1 = 74HC595 [package="DIP16 [THT]"]
  U2 = 74HC595 [package="DIP16 [THT]"]
  R1 = Resistor [tolerance=±5% resistance=220 package=THT]
  R2 = Resistor [tolerance=±5% resistance=220 package=THT]
  R3 = Resistor [tolerance=±5% resistance=220 package=THT]
  R4 = Resistor [tolerance=±5% resistance=220 package=THT]
  R5 = Resistor [tolerance=±5% resistance=220 package=THT]
  R6 = Resistor [tolerance=±5% resistance=220 package=THT]
  R7 = Resistor [tolerance=±5% resistance=220 package=THT]
  R9 = Resistor [tolerance=±5% resistance=220 package=THT]
  R10 = Resistor [tolerance=±5% resistance=220 package=THT]
  R11 = Resistor [tolerance=±5% resistance=220 package=THT]
  R12 = Resistor [tolerance=±5% resistance=220 package=THT]
  R13 = Resistor [tolerance=±5% resistance=220 package=THT]
  R14 = Resistor [tolerance=±5% resistance=220 package=THT]
  R16 = Resistor [tolerance=±5% resistance=220 package=THT]
  7_Segment1 = 7 Segment Display
  7_Segment2 = 7 Segment Display
  Componente1 = Arduino Uno (Rev3)

nets (from the breadboard view):
  N1: U1.Q1, R1.Pin_1
  N2: U1.Q2, R2.Pin_1
  N3: U1.Q3, R3.Pin_1
  N4: U1.Q4, R4.Pin_0
  N5: U1.Q5, R5.Pin_0
  N6: U1.Q6, R6.Pin_0
  GND: U1.GND, U1.OE, U2.GND, U2.OE, 7_Segment1.common_anode, 7_Segment2.common_anode, Componente1.GND
  N7: U1.Q7', U2.DS
  VCC: U1.MR, U1.VCC, U2.MR, U2.VCC, Componente1.5V
  N8: U1.SH_CP, U2.SH_CP, Componente1.D2
  N9: U1.ST_CP, U2.ST_CP, Componente1.D3_PWM
  N10: U1.DS, Componente1.D4
  N11: U1.Q0, R7.Pin_1
  N12: U2.Q1, R9.Pin_1
  N13: U2.Q2, R10.Pin_1
  N14: U2.Q3, R11.Pin_1
  N15: U2.Q4, R12.Pin_0
  N16: U2.Q5, R13.Pin_0
  N17: U2.Q6, R14.Pin_0
  N18: U2.Q0, R16.Pin_1
  N19: R1.Pin_0, 7_Segment1.Segment_G
  N20: R2.Pin_0, 7_Segment1.Segment_B
  N21: R3.Pin_0, 7_Segment1.Segment_C
  N22: R4.Pin_1, 7_Segment1.Segment_DP
  N23: R5.Pin_1, 7_Segment1.Segment_E
  N24: R6.Pin_1, 7_Segment1.Segment_D
  N25: R7.Pin_0, 7_Segment1.Segment_F
  N26: R9.Pin_0, 7_Segment2.Segment_G
  N27: R10.Pin_0, 7_Segment2.Segment_B
  N28: R11.Pin_0, 7_Segment2.Segment_C
  N29: R12.Pin_1, 7_Segment2.Segment_DP
  N30: R13.Pin_1, 7_Segment2.Segment_E
  N31: R14.Pin_1, 7_Segment2.Segment_D
  N32: R16.Pin_0, 7_Segment2.Segment_F
