# Fritzing sketch ldr_led (saved by Fritzing 0.9.3b)
breadboards: 1

parts:
  R1 = Photocell (LDR) [package=THT]
  R2 = Resistor [tolerance=±5% resistance=220 package=THT]
  LED1 = LED - 5mm [color="Red (633nm)" package="5 mm [THT]"]
  LED2 = LED - 5mm [color="Red (633nm)" package="5 mm [THT]"]
  LED3 = LED - 5mm [color="Red (633nm)" package="5 mm [THT]"]
  R3 = Resistor [tolerance=±5% resistance=220 package=THT]
  R4 = Resistor [tolerance=±5% resistance=220 package=THT]
  R5 = Resistor [tolerance=±5% resistance=220 package=THT]
  Componente1 = Arduino Uno (Rev3)

nets:
  N1: R1.pin_0, R2.Pin_1, Componente1.A0
  N2: R1.pin_1, Componente1.5V
  N3: R2.Pin_0, LED1.cathode, LED2.cathode, LED3.cathode, Componente1.GND
  N4: LED1.anode, R3.Pin_0
  N5: LED2.anode, R4.Pin_0
  N6: LED3.anode, R5.Pin_0
  N7: R3.Pin_1, Componente1.D11_PWM/MOSI
  N8: R4.Pin_1, Componente1.D10_PWM/SS
  N9: R5.Pin_1, Componente1.D9_PWM
