# Fritzing sketch thermistor+buzzer (saved by Fritzing 0.9.3b)
breadboards: 1

parts:
  T1 = LM35 Temperature Sensor [package="TO92 [THT]"]
  R1 = Resistor [tolerance=±5% resistance=10k package=THT]
  J1 = Piezo Speaker
  Componente1 = Arduino Uno (Rev3)

nets:
  N1: T1.+Vs, Componente1.5V
  N2: T1.GND, R1.Pin_0, Componente1.A0
  N3: R1.Pin_1, J1.pin1, Componente1.GND
  N4: J1.pin2, Componente1.D11_PWM/MOSI
