# Fritzing sketch four_digitalv2 (saved by Fritzing 0.9.3b)
breadboards: 1

parts:
  LED1 = 7-SEGMENT-4DIGIT-YOUNGSUN [package=7-segment-4digit-youngsun-longpads]
  R1 = Resistor [tolerance=±5% resistance=220 package=THT]
  R2 = Resistor [tolerance=±5% resistance=220 package=THT]
  R3 = Resistor [tolerance=±5% resistance=220 package=THT]
  R4 = Resistor [tolerance=±5% resistance=220 package=THT]
  R5 = Resistor [tolerance=±5% resistance=220 package=THT]
  R6 = Resistor [tolerance=±5% resistance=220 package=THT]
  R7 = Resistor [tolerance=±5% resistance=220 package=THT]
  Componente1 = Arduino Uno (Rev3)

nets:
  N1: LED1.DIG2, R3.Pin_1
  N2: LED1.D, R2.Pin_1
  N3: LED1.E, R1.Pin_1
  N4: LED1.DIG3, R7.Pin_1
  N5: LED1.DP, Componente1.D12/MISO
  N6: LED1.APOS-A, R5.Pin_0
  N7: LED1.F, Componente1.D11_PWM/MOSI
  N8: LED1.COL-C, Componente1.D10_PWM/SS
  N9: LED1.C, R4.Pin_0
  N10: LED1.A, R6.Pin_0
  N11: LED1.G, Componente1.D9_PWM
  N12: R1.Pin_0, Componente1.D4
  N13: R2.Pin_0, Componente1.D5_PWM
  N14: R3.Pin_0, Componente1.D6_PWM
  N15: R4.Pin_1, Componente1.D7
  N16: R5.Pin_1, Componente1.D3_PWM
  N17: R6.Pin_1, Componente1.D2
  N18: R7.Pin_0, Componente1.D8
