# Fritzing sketch semaforo-peatones (saved by Fritzing 0.9.3b)
breadboards: 1

parts:
  Componente1 = Arduino Uno (Rev3)
  LED1 = LED - 5mm [color="Green (560nm)" package="5 mm [THT]"]
  LED2 = LED - 5mm [color="Red (633nm)" package="5 mm [THT]"]
  R1 = Resistor [tolerance=±5% resistance=220 package=THT]
  R2 = Resistor [tolerance=±5% resistance=220 package=THT]
  J1 = Piezo Speaker

nets:
  N1: Componente1.GND, LED1.cathode, LED2.cathode, J1.pin1
  N2: Componente1.D3_PWM, J1.pin2
  N3: Componente1.D4, R1.Pin_1
  N4: Componente1.D5_PWM, R2.Pin_1
  N5: LED1.anode, R2.Pin_0
  N6: LED2.anode, R1.Pin_0
